# Fritzing sketch RGBLEDModule (saved by Fritzing 0.9.2b)

parts:
  元件1 = Adeept RGB LED Module [part_number="Adeept RGB LED Module"]
  元件2 = Adeept Uno (Rev3)

nets:
  N1: 元件1.R, 元件2.D11_PWM/MOSI
  N2: 元件1.+, 元件2.5V
  N3: 元件1.G, 元件2.D10_PWM/SS
  N4: 元件1.B, 元件2.D9_PWM

custom parts:
  Adeept Uno (Rev3): The Adeept Uno is a microcontroller board based on the ATmega328 (datasheet). It has 14 digital input/output pins (of which 6 can be used as PWM outputs), 6 analog inputs, a 16 MHz ceramic resonator, a USB connection, a power jack, an ICSP header, and a reset button. It contains everything needed to support the microcontroller; simply connect it to a computer with a USB cable or power it with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
