# Fritzing sketch TermistorModule (saved by Fritzing 0.9.2b)

parts:
  元件2 = Adeept MIC Module [part_number="Adeept MIC Module"]
  元件3 = Adeept Uno (Rev3)

nets:
  N1: 元件2.-, 元件3.GND
  N2: 元件2.+, 元件3.5V
  N3: 元件2.A, 元件3.A0

custom parts:
  Adeept Uno (Rev3): The Adeept Uno is a microcontroller board based on the ATmega328 (datasheet). It has 14 digital input/output pins (of which 6 can be used as PWM outputs), 6 analog inputs, a 16 MHz ceramic resonator, a USB connection, a power jack, an ICSP header, and a reset button. It contains everything needed to support the microcontroller; simply connect it to a computer with a USB cable or power it with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
