# Fritzing sketch LCD1602Module (saved by Fritzing 0.9.2b)

parts:
  元件1 = Adeept Uno (Rev3)
  元件3 = Adeept Potentiometer Module [part_number="Adeept Potentiometer Module"]
  元件4 = Adeept Breadboard [part_number="Adeept Breadboard"]
  LCD1 = LCD screen

nets:
  N1: 元件1.D10_PWM/SS, LCD1.DB4
  N2: 元件1.D11_PWM/MOSI, LCD1.DB5
  N3: 元件1.D12/MISO, LCD1.DB6
  N4: 元件1.D13/SCK, LCD1.DB7
  N5: 元件1.D4, LCD1.RS
  N6: 元件1.D6_PWM, LCD1.E
  5V: 元件1.5V, 元件3.+, 元件4.pin_0, 元件4.pin_7, 元件4.pin_9, 元件4.pin_19, LCD1.VDD, LCD1.LED+
  GND: 元件1.GND, 元件3.-, 元件4.pin_29, 元件4.pin_39, 元件4.pin_41, 元件4.pin_43, 元件4.pin_49, LCD1.VSS, LCD1.R/W, LCD1.LED-
  N7: 元件3.A, 元件4.pin_115, 元件4.pin_116, LCD1.V0

custom parts:
  Adeept Uno (Rev3): The Adeept Uno is a microcontroller board based on the ATmega328 (datasheet). It has 14 digital input/output pins (of which 6 can be used as PWM outputs), 6 analog inputs, a 16 MHz ceramic resonator, a USB connection, a power jack, an ICSP header, and a reset button. It contains everything needed to support the microcontroller; simply connect it to a computer with a USB cable or power it with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
