# Fritzing sketch IICInterfaceModule (saved by Fritzing 0.9.2b)

parts:
  元件1 = Adeept IIC Interface Module [part_number="Adeept IIC Interface Module"]
  元件2 = Adeept Uno (Rev3)
  LCD1 = LCD screen

nets:
  N1: 元件1.SDA, 元件2.A4/SDA
  VDD: 元件1.+, 元件1.VDD, 元件2.5V, LCD1.VDD
  VSS: 元件1.-, 元件1.VSS, 元件2.GND, LCD1.VSS
  N2: 元件1.SCL, 元件2.A5/SCL
  N3: 元件1.VO, LCD1.V0
  N4: 元件1.RS, LCD1.RS
  N5: 元件1.RW, LCD1.R/W
  N6: 元件1.E, LCD1.E
  N7: 元件1.D0, LCD1.DB0
  N8: 元件1.D1, LCD1.DB1
  N9: 元件1.D2, LCD1.DB2
  N10: 元件1.D3, LCD1.DB3
  N11: 元件1.D4, LCD1.DB4
  N12: 元件1.D5, LCD1.DB5
  N13: 元件1.D6, LCD1.DB6
  N14: 元件1.D7, LCD1.DB7
  N15: 元件1.A, LCD1.LED+
  N16: 元件1.K, LCD1.LED-

custom parts:
  Adeept Uno (Rev3): The Adeept Uno is a microcontroller board based on the ATmega328 (datasheet). It has 14 digital input/output pins (of which 6 can be used as PWM outputs), 6 analog inputs, a 16 MHz ceramic resonator, a USB connection, a power jack, an ICSP header, and a reset button. It contains everything needed to support the microcontroller; simply connect it to a computer with a USB cable or power it with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
