# Fritzing sketch LaserReceiverModule (saved by Fritzing 0.9.2b)

parts:
  元件1 = Adeept Laser Receiver Module [part_number="Adeept Laser Receiver Module"]
  元件2 = Adeept Uno (Rev3)
  元件3 = Adeept Breadboard [part_number="Adeept Breadboard"]
  元件4 = Adeept Laser Transmitter Module [part_number="Adeept Laser Transmitter Module"]

nets:
  N1: 元件1.S, 元件2.D7
  N2: 元件1.+, 元件2.5V, 元件3.pin_320, 元件3.pin_324, 元件3.pin_342, 元件3.pin_346, 元件4.S, 元件4.+
  N3: 元件1.-, 元件2.GND, 元件3.pin_325, 元件3.pin_341, 元件3.pin_349, 元件4.-

custom parts:
  Adeept Uno (Rev3): The Adeept Uno is a microcontroller board based on the ATmega328 (datasheet). It has 14 digital input/output pins (of which 6 can be used as PWM outputs), 6 analog inputs, a 16 MHz ceramic resonator, a USB connection, a power jack, an ICSP header, and a reset button. It contains everything needed to support the microcontroller; simply connect it to a computer with a USB cable or power it with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
