# Fritzing sketch RelayModule (saved by Fritzing 0.9.2b)

parts:
  元件1 = Adeept Uno (Rev3)
  元件2 = Adeept Red LED Module [part_number="Adeept Red LED Module"]
  元件3 = Adeept Relay Module [part_number="Adeept  Relay Module"]
  元件4 = Adeept Breadboard [part_number="Adeept Breadboard"]

nets:
  N1: 元件1.D8, 元件3.S
  N2: 元件1.5V, 元件2.+, 元件3.+, 元件3.VCC1, 元件3.VCC2, 元件4.pin_320, 元件4.pin_324, 元件4.pin_366
  GND: 元件1.GND, 元件3.-, 元件3.GND1, 元件3.GND2, 元件4.pin_325, 元件4.pin_329, 元件4.pin_369

custom parts:
  Adeept Uno (Rev3): The Adeept Uno is a microcontroller board based on the ATmega328 (datasheet). It has 14 digital input/output pins (of which 6 can be used as PWM outputs), 6 analog inputs, a 16 MHz ceramic resonator, a USB connection, a power jack, an ICSP header, and a reset button. It contains everything needed to support the microcontroller; simply connect it to a computer with a USB cable or power it with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
