# Fritzing sketch simpleLaserPen (saved by Fritzing 0.9.2b)

parts:
  元件1 = Adeept Red Button Module [part_number="Adeept Red Button Module"]
  元件3 = Adeept Uno (Rev3)
  元件4 = Adeept Breadboard [part_number="Adeept Breadboard"]
  Part1 = Adeept Laser Transmitter Module [part_number="Adeept Laser Transmitter Module"]

nets:
  N1: 元件1.S, 元件3.D2
  N2: 元件1.+, 元件3.5V, 元件4.pin_320, 元件4.pin_334, 元件4.pin_360, Part1.+
  N3: 元件1.-, 元件3.GND, 元件4.pin_325, 元件4.pin_331, 元件4.pin_365, Part1.-
  N4: 元件3.D11_PWM/MOSI, Part1.S

custom parts:
  Adeept Uno (Rev3): The Adeept Uno is a microcontroller board based on the ATmega328 (datasheet). It has 14 digital input/output pins (of which 6 can be used as PWM outputs), 6 analog inputs, a 16 MHz ceramic resonator, a USB connection, a power jack, an ICSP header, and a reset button. It contains everything needed to support the microcontroller; simply connect it to a computer with a USB cable or power it with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
