# Fritzing sketch smallPianist (saved by Fritzing 0.9.2b)

parts:
  元件2 = Adeept White Button Module [part_number="Adeept White Button Module"]
  元件3 = Adeept Uno (Rev3)
  元件4 = Adeept Breadboard [part_number="Adeept Breadboard"]
  元件5 = Adeept Blue Button Module [part_number="Adeept Blue Button Module"]
  元件6 = Adeept Blue Button Module [part_number="Adeept Blue Button Module"]
  元件1 = Adeept Red Button Module [part_number="Adeept Red Button Module"]
  Part1 = Adeept Passive Buzzer Module [part_number="Adeept Passive Buzzer Module"]
  Part2 = Adeept Slide Potentionmeter Module [part_number="Adeept Slide Potentionmeter Module"]

nets:
  N1: 元件2.S, 元件3.D0/RX
  N2: 元件2.+, 元件3.5V, 元件4.pin_0, 元件4.pin_1, 元件4.pin_2, 元件4.pin_3, 元件4.pin_5, 元件4.pin_7, 元件4.pin_8, 元件5.+, 元件6.+, 元件1.+, Part1.+, Part2.+
  N3: 元件2.-, 元件3.GND, 元件4.pin_40, 元件4.pin_41, 元件4.pin_45, 元件4.pin_46, 元件4.pin_47, 元件4.pin_48, 元件4.pin_49, 元件5.-, 元件6.-, 元件1.-, Part1.-, Part2.-
  N4: 元件3.A0, Part2.A
  N5: 元件3.D12/MISO, 元件5.S
  N6: 元件3.D13/SCK, 元件6.S
  N7: 元件3.D1/TX, 元件1.S
  N8: 元件3.D5_PWM, Part1.S

custom parts:
  Adeept Uno (Rev3): The Adeept Uno is a microcontroller board based on the ATmega328 (datasheet). It has 14 digital input/output pins (of which 6 can be used as PWM outputs), 6 analog inputs, a 16 MHz ceramic resonator, a USB connection, a power jack, an ICSP header, and a reset button. It contains everything needed to support the microcontroller; simply connect it to a computer with a USB cable or power it with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
