# Fritzing sketch dht_11AlarmViaBuzzer (saved by Fritzing 0.9.2b)

parts:
  元件1 = Adeept DHT-11 Sensor Module [part_number="Adeept DHT-11 Sensor Module"]
  元件2 = Adeept Uno (Rev3)
  Part1 = Adeept Breadboard [part_number="Adeept Breadboard"]
  Part2 = Adeept Passive Buzzer Module [part_number="Adeept Passive Buzzer Module"]

nets:
  N1: 元件1.S, 元件2.D2
  N2: 元件1.+, 元件2.5V, Part1.pin_180, Part1.pin_182, Part1.pin_184, Part2.+
  N3: 元件1.-, 元件2.GND, Part1.pin_315, Part1.pin_317, Part1.pin_319, Part2.-
  N4: 元件2.D5_PWM, Part2.S

custom parts:
  Adeept Uno (Rev3): The Adeept Uno is a microcontroller board based on the ATmega328 (datasheet). It has 14 digital input/output pins (of which 6 can be used as PWM outputs), 6 analog inputs, a 16 MHz ceramic resonator, a USB connection, a power jack, an ICSP header, and a reset button. It contains everything needed to support the microcontroller; simply connect it to a computer with a USB cable or power it with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
