# Fritzing sketch MQ_2AlarmViaBuzzer (saved by Fritzing 0.9.2b)

parts:
  元件1 = Adeept Uno (Rev3)
  Part1 = Adeept MQ-2 Gas Sensor Module [part_number="Adeept MQ-2 Gas Sensor Module"]
  Part2 = Adeept Breadboard [part_number="Adeept Breadboard"]
  Part3 = Adeept Passive Buzzer Module [part_number="Adeept Passive Buzzer Module"]

nets:
  N1: 元件1.A1, Part1.A
  N2: 元件1.D5_PWM, Part3.S
  N3: 元件1.D7, Part1.S
  N4: 元件1.5V, Part1.+, Part2.pin_180, Part2.pin_181, Part2.pin_184, Part3.+
  N5: 元件1.GND, Part1.-, Part2.pin_315, Part2.pin_317, Part2.pin_319, Part3.-

custom parts:
  Adeept Uno (Rev3): The Adeept Uno is a microcontroller board based on the ATmega328 (datasheet). It has 14 digital input/output pins (of which 6 can be used as PWM outputs), 6 analog inputs, a 16 MHz ceramic resonator, a USB connection, a power jack, an ICSP header, and a reset button. It contains everything needed to support the microcontroller; simply connect it to a computer with a USB cable or power it with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
