# Fritzing sketch led_Processing (saved by Fritzing 0.9.2b)

parts:
  元件1 = Adeept Breadboard [part_number="Adeept Breadboard"]
  元件2 = Adeept Uno (Rev3)
  元件3 = Adeept Red LED Module [part_number="Adeept Red LED Module"]
  元件4 = Adeept Green LED Module [part_number="Adeept Green LED Module"]
  元件5 = Adeept Yellow LED Module [part_number="Adeept Yellow LED Module"]
  元件6 = Adeept Blue LED Module [part_number="Adeept Blue LED Module"]

nets:
  N1: 元件1.pin_29, 元件1.pin_43, 元件1.pin_45, 元件1.pin_46, 元件1.pin_49, 元件2.GND, 元件3.-, 元件4.-, 元件5.-, 元件6.-
  N2: 元件2.D8, 元件3.+
  N3: 元件2.D9_PWM, 元件4.+
  N4: 元件2.D10_PWM/SS, 元件6.+
  N5: 元件2.D11_PWM/MOSI, 元件5.+

custom parts:
  Adeept Uno (Rev3): The Adeept Uno is a microcontroller board based on the ATmega328 (datasheet). It has 14 digital input/output pins (of which 6 can be used as PWM outputs), 6 analog inputs, a 16 MHz ceramic resonator, a USB connection, a power jack, an ICSP header, and a reset button. It contains everything needed to support the microcontroller; simply connect it to a computer with a USB cable or power it with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
