# Fritzing sketch Button_Processing (saved by Fritzing 0.9.2b)

parts:
  元件1 = Adeept Red Button Module [part_number="Adeept Red Button Module"]
  元件2 = Adeept White Button Module [part_number="Adeept White Button Module"]
  元件3 = Adeept Uno (Rev3)
  元件4 = Adeept Breadboard [part_number="Adeept Breadboard"]
  元件5 = Adeept Blue Button Module [part_number="Adeept Blue Button Module"]
  元件6 = Adeept Blue Button Module [part_number="Adeept Blue Button Module"]

nets:
  N1: 元件1.S, 元件3.D8
  N2: 元件1.+, 元件2.+, 元件3.5V, 元件4.pin_0, 元件4.pin_5, 元件4.pin_7, 元件4.pin_10, 元件4.pin_22, 元件5.+, 元件6.+
  N3: 元件1.-, 元件2.-, 元件3.GND, 元件4.pin_26, 元件4.pin_38, 元件4.pin_41, 元件4.pin_43, 元件4.pin_49, 元件5.-, 元件6.-
  N4: 元件2.S, 元件3.D9_PWM
  N5: 元件3.D10_PWM/SS, 元件5.S
  N6: 元件3.D11_PWM/MOSI, 元件6.S

custom parts:
  Adeept Uno (Rev3): The Adeept Uno is a microcontroller board based on the ATmega328 (datasheet). It has 14 digital input/output pins (of which 6 can be used as PWM outputs), 6 analog inputs, a 16 MHz ceramic resonator, a USB connection, a power jack, an ICSP header, and a reset button. It contains everything needed to support the microcontroller; simply connect it to a computer with a USB cable or power it with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
